// Logisim project mac.circ as structural Verilog: 5 circuits, main circuit main
module main (
);

  wire clk, comparator_1_eq, not_1_out, ram_en, rd_mem, rst;
  wire [2:0] sel_mac, sel_op;
  wire [4:0] rgb_video_1_p4, rgb_video_1_p5;
  wire [7:0] rom_img_data;
  wire [9:0] counter_3_q;
  wire [15:0] counter_1_q, ld_a_0, ld_a_1, ld_a_2, ld_a_3, ld_a_4, ld_a_5, ld_a_6, ld_a_7, ld_b_0, ld_b_1,
       ld_b_2, ld_b_3, ld_b_4, ld_b_5, ld_b_6, ld_b_7, op0, op1, op2, op3, op4, op5, op6, op7, w0, w1, w2,
       w3, w4, w5, w6, w7;
  wire [31:0] data_bus, ram_64k_32_dout, random_input_1_random_number;

  // Probe on ld_b_0
  // Probe on ld_a_0
  // Probe on ld_b_4
  // Probe on ld_a_4
  // DipSwitch #(.number(2)) switch: pin names not known; wires that end beside it: rd_mem, ram_en, 1'b1
  Button u_rst (.out(rst));
  Clock clock_1 (.out(clk));
  mac mac_0 (.a(ld_a_0), .b(ld_b_0), .clk(clk), .rst(rst), .op(op0));
  mac mac_4 (.a(ld_a_4), .b(ld_b_4), .clk(clk), .rst(rst), .op(op4));
  Counter #(.max('hffff), .width(16)) counter_1 (
    .load(1'b0), .D({16{1'b0}}), .count(1'b1), .Q(counter_1_q), .up(1'b1), .clk(clk), .clr(rst));  // open: carry
  not not_1 (not_1_out, rd_mem);
  // Probe on random_input_1_random_number
  random_input random_input_1 (.rst(rst), .clk(clk), .random_number(random_input_1_random_number));
  // Probe on op0
  // Probe on op4
  Multiplexer #(.select(3), .width(32)) multiplexer_1 (
    .in0({w0, op0}), .in1({w1, op1}), .in2({w2, op2}), .in3({w3, op3}), .in4({w4, op4}), .in5({w5, op5}),
    .in6({w6, op6}), .in7({w7, op7}), .out(data_bus), .sel(sel_op));
  // Probe on data_bus
  RAM #(.addrWidth(16), .dataWidth(32)) ram_64k_32 (
    .addr(counter_1_q), .we(not_1_out), .oe(rd_mem), .clk(clk), .din(random_input_1_random_number),
    .dout(ram_64k_32_dout));
  // Probe on ld_b_1
  // Probe on ld_b_5
  // Probe on sel_mac
  // Probe on ld_a_1
  // Probe on ld_a_5
  Demultiplexer #(.select(3), .width(32)) demultiplexer_1 (
    .out0({ld_a_0, ld_b_0}), .out1({ld_a_1, ld_b_1}), .out2({ld_a_2, ld_b_2}), .out3({ld_a_3, ld_b_3}),
    .out4({ld_a_4, ld_b_4}), .out5({ld_a_5, ld_b_5}), .out6({ld_a_6, ld_b_6}), .out7({ld_a_7, ld_b_7}),
    .in(data_bus), .sel(sel_mac));
  // Probe on ram_64k_32_dout[31:16]
  // Probe on ram_64k_32_dout[15:0]
  Counter #(.max('h7), .width(3)) counter_2 (.Q(sel_mac), .clk(clk));  // open: load, D, count, carry, up, clr
  assign data_bus = ram_en ? ram_64k_32_dout : 32'bz;  // Controlled_Buffer controlled_buffer_1
  // Probe on op1
  mac mac_1 (.a(ld_a_1), .b(ld_b_1), .clk(clk), .rst(rst), .op(op1));
  // Probe on op5
  mac mac_5 (.a(ld_a_5), .b(ld_b_5), .clk(clk), .rst(rst), .op(op5));
  // Probe on ld_b_2
  // Probe on ld_b_6
  ROM #(.addrWidth(10)) rom_img (.addr(counter_3_q), .data(rom_img_data));
  // Probe on ld_a_2
  // Probe on ld_a_6
  Counter #(.max('h3ff), .width(10)) counter_3 (
    .Q(counter_3_q), .clk(clk), .clr(rst));  // open: load, D, count, carry, up
  // Probe on op2
  mac mac_2 (.a(ld_a_2), .b(ld_b_2), .clk(clk), .rst(rst), .op(op2));
  // Probe on op6
  mac mac_6 (.a(ld_a_6), .b(ld_b_6), .clk(clk), .rst(rst), .op(op6));
  // Probe on ld_b_3
  // Probe on ld_b_7
  // RGB_Video #(.height(32), .scale(8), .width(32)) rgb_video_1: pin names not known; wires that end beside it: rst, clk, 1'b1, rgb_video_1_p4, rgb_video_1_p5, {{16{1'b0}}, rom_img_data}
  Counter #(.max('h1f), .width(5)) x_cdnt (
    .Q(rgb_video_1_p4), .clk(clk), .clr(rst));  // open: load, D, count, carry, up
  // Probe on ld_a_3
  // Probe on ld_a_7
  Comparator #(.width(5)) comparator_1 (.a(rgb_video_1_p4), .b({5{1'b1}}), .eq(comparator_1_eq));  // open: gt, lt
  Counter #(.max('h1f), .width(5)) y_cdnt (
    .Q(rgb_video_1_p5), .clk(comparator_1_eq), .clr(rst));  // open: load, D, count, carry, up
  // Probe on op3
  mac mac_3 (.a(ld_a_3), .b(ld_b_3), .clk(clk), .rst(rst), .op(op3));
  // Probe on op7
  mac mac_7 (.a(ld_a_7), .b(ld_b_7), .clk(clk), .rst(rst), .op(op7));

  // Notes on the sheet:
  //   contents of rom_img (hex, n*v repeats v):
  //   230*0 54 b9 9f 97 3c 24 26*0 de 4*fe f1 8*c6 aa 34 16*0 43 72 48 72 a3 e3 fe e1 fe fe fe fa e5 fe fe
  //   8c 21*0 11 42 e 43 43 43 3b 15 ec fe 6a 28*0 53 fd d1 12 27*0 16 e9 ff 53 28*0 81 fe ee 2c 27*0 3b
  //   f9 fe 3e 28*0 85 fe bb 5 27*0 9 cd f8 3a 28*0 7e fe b6 28*0 4b fb f0 39 27*0 13 dd fe a6 27*0 3 cb
  //   fe db 23 27*0 26 fe fe 4d 27*0 1f e0 fe 73 1 27*0 85 fe fe 34 27*0 3d f2 fe fe 34 27*0 79 fe fe db
  //   28 27*0 79 fe cf 12
endmodule

module mac (
  input  [15:0] a,
  input  [15:0] b,
  input  clk,
  input  rst,
  output [15:0] op
);

  wire not_1_out;
  wire [15:0] bit_extender_1_out, multiplexer_1_out, multiplexer_2_out, multiplier_1_out;

  assign bit_extender_1_out = {{15{1'b0}}, 1'b0};  // Bit_Extender bit_extender_1
  // Probe on a
  // Probe on b
  Multiplexer #(.width(16)) multiplexer_1 (.in0(bit_extender_1_out), .in1(a), .out(multiplexer_1_out), .sel(not_1_out));
  Multiplexer #(.width(16)) multiplexer_2 (.in0(bit_extender_1_out), .in1(b), .out(multiplexer_2_out), .sel(not_1_out));
  not not_1 (not_1_out, rst);
  // Probe on multiplier_1_out
  Multiplier #(.width(16)) multiplier_1 (
    .a(multiplexer_1_out), .b(multiplexer_2_out), .out(multiplier_1_out), .cin(op));  // open: cout
  // Probe on op
  Register #(.width(16)) register_1 (.D(multiplier_1_out), .en(1'b1), .clk(clk), .Q(op), .clr(rst));
endmodule

module random_input (
  input  rst,
  input  clk,
  output [31:0] random_number
);

  wire random_1_out;

  Random #(.width(1)) random_1 (.clk(clk), .out(random_1_out));  // open: clr, next
  Random random_2 (.clr(rst), .next(random_1_out), .clk(clk), .out(random_number[7:0]));
  Random random_3 (.clr(rst), .clk(clk), .out(random_number[23:16]));  // open: next
  // Probe on random_number[7:0]
  // Probe on random_number[23:16]
  // Probe on {{8{1'b0}}, random_number[7:0]}
  // Probe on {{8{1'b0}}, random_number[23:16]}
  // Probe on {{8{1'b0}}, random_number[23:16], {8{1'b0}}, random_number[7:0]}

  assign {random_number[31:24], random_number[15:8]} = {16{1'b0}};
endmodule

module mac_p (
  input  [63:0] w0,
  input  [63:0] x0,
  input  [63:0] w1,
  input  [63:0] x1,
  input  [7:0] b,
  input  latch,
  input  en_bar,
  output [7:0] opt
);

  wire ad0, ad1, ad2, ad3, ad4, ad5, ad6, ad7, ad8, ad9, ad10, ad11, ad12, ad13, ad14, ad15, c0, c1, c2,
       comparator_1_eq, comparator_2_eq, comparator_3_eq, op_or;
  wire [7:0] adder_1_out, adder_2_out, adder_3_out, adder_4_out, adder_5_out, adder_6_out, adder_7_out,
       adder_8_out, adder_9_out, adder_10_out, adder_11_out, adder_12_out, adder_13_out, adder_14_out,
       adder_15_out, adder_16_out, multiplexer_1_out, multiplier_1_cout, multiplier_1_out, multiplier_2_cout,
       multiplier_2_out, multiplier_3_cout, multiplier_3_out, multiplier_4_cout, multiplier_4_out,
       multiplier_5_cout, multiplier_5_out, multiplier_6_out, multiplier_7_out, multiplier_8_out,
       multiplier_9_cout, multiplier_9_out, multiplier_10_cout, multiplier_10_out, multiplier_11_cout,
       multiplier_11_out, multiplier_12_cout, multiplier_12_out, multiplier_13_out, multiplier_14_out,
       multiplier_15_out, multiplier_16_out;
  wire [23:0] multiplier_8_cout;
  wire [39:0] multiplier_15_cout;

  not not_1 (c2, comparator_1_eq);
  Comparator #(.width(16)) comparator_1 (
    .a({16{1'b0}}),
    .b({ad0, ad1, ad2, ad3, ad4, ad5, ad6, ad7, ad8, ad9, ad10, ad11, ad12, ad13, ad14, ad15}),
    .eq(comparator_1_eq));  // open: gt, lt
  Multiplier multiplier_1 (.a(w0[7:0]), .b(x0[7:0]), .out(multiplier_1_out), .cout(multiplier_1_cout));  // open: cin
  Multiplier multiplier_2 (.a(w0[15:8]), .b(x0[15:8]), .out(multiplier_2_out), .cout(multiplier_2_cout));  // open: cin
  Multiplier multiplier_3 (
    .a(w0[23:16]), .b(x0[23:16]), .out(multiplier_3_out), .cout(multiplier_3_cout));  // open: cin
  Multiplier multiplier_4 (
    .a(w0[31:24]), .b(x0[31:24]), .out(multiplier_4_out), .cout(multiplier_4_cout));  // open: cin
  Multiplier multiplier_5 (
    .a(w0[39:32]), .b(x0[39:32]), .out(multiplier_5_out), .cout(multiplier_5_cout));  // open: cin
  Multiplier multiplier_6 (
    .a(w0[47:40]), .b(x0[47:40]), .out(multiplier_6_out), .cout(multiplier_8_cout[23:16]));  // open: cin
  Multiplier multiplier_7 (
    .a(w0[55:48]), .b(x0[55:48]), .out(multiplier_7_out), .cout(multiplier_8_cout[15:8]));  // open: cin
  Multiplier multiplier_8 (
    .a(w0[63:56]), .b(x0[63:56]), .out(multiplier_8_out), .cout(multiplier_8_cout[7:0]));  // open: cin
  not not_2 (c0, comparator_2_eq);
  Comparator #(.width(64)) comparator_2 (
    .a({multiplier_1_cout, multiplier_2_cout, multiplier_3_cout, multiplier_4_cout, multiplier_5_cout, multiplier_8_cout}),
    .b({64{1'b0}}), .eq(comparator_2_eq));  // open: gt, lt
  or or_1 (op_or, c0, c1, c2);
  Adder adder_1 (.a(multiplier_1_out), .b(multiplier_2_out), .out(adder_1_out), .cout(ad0));  // open: cin
  Adder adder_2 (.a(multiplier_3_out), .b(multiplier_4_out), .out(adder_2_out), .cout(ad1));  // open: cin
  Adder adder_3 (.a(multiplier_5_out), .b(multiplier_6_out), .out(adder_3_out), .cout(ad2));  // open: cin
  Adder adder_4 (.a(multiplier_7_out), .b(multiplier_8_out), .out(adder_4_out), .cout(ad3));  // open: cin
  Adder adder_5 (.a(adder_1_out), .b(adder_2_out), .out(adder_5_out), .cout(ad4));  // open: cin
  Adder adder_6 (.a(adder_3_out), .b(adder_4_out), .out(adder_6_out), .cout(ad5));  // open: cin
  Adder adder_7 (.a(adder_5_out), .b(adder_6_out), .out(adder_7_out), .cout(ad6));  // open: cin
  Adder adder_8 (.a(adder_7_out), .b(adder_16_out), .out(adder_8_out), .cout(ad14));  // open: cin
  not not_3 (c1, comparator_3_eq);
  Comparator #(.width(64)) comparator_3 (
    .a({multiplier_9_cout, multiplier_10_cout, multiplier_11_cout, multiplier_15_cout[39:32], multiplier_12_cout, multiplier_15_cout[23:0]}),
    .b({64{1'b0}}), .eq(comparator_3_eq));  // open: gt, lt
  Multiplier multiplier_9 (.a(w1[7:0]), .b(x1[7:0]), .out(multiplier_9_out), .cout(multiplier_9_cout));  // open: cin
  Multiplier multiplier_10 (
    .a(w1[15:8]), .b(x1[15:8]), .out(multiplier_10_out), .cout(multiplier_10_cout));  // open: cin
  Multiplier multiplier_11 (
    .a(w1[23:16]), .b(x1[23:16]), .out(multiplier_11_out), .cout(multiplier_11_cout));  // open: cin
  Multiplier multiplier_12 (
    .a(w1[31:24]), .b(x1[31:24]), .out(multiplier_12_out), .cout(multiplier_12_cout));  // open: cin
  Multiplier multiplier_13 (
    .a(w1[39:32]), .b(x1[39:32]), .out(multiplier_13_out), .cout(multiplier_15_cout[23:16]));  // open: cin
  Multiplier multiplier_14 (
    .a(w1[47:40]), .b(x1[47:40]), .out(multiplier_14_out), .cout(multiplier_15_cout[15:8]));  // open: cin
  Multiplier multiplier_15 (
    .a(w1[55:48]), .b(x1[55:48]), .out(multiplier_15_out), .cout(multiplier_15_cout[7:0]));  // open: cin
  Multiplier multiplier_16 (
    .a(w1[63:56]), .b(x1[63:56]), .out(multiplier_16_out), .cout(multiplier_15_cout[39:32]));  // open: cin
  Adder adder_9 (.a(adder_8_out), .b(b), .out(adder_9_out), .cout(ad15));  // open: cin
  Adder adder_10 (.a(multiplier_9_out), .b(multiplier_10_out), .out(adder_10_out), .cout(ad7));  // open: cin
  Adder adder_11 (.a(multiplier_11_out), .b(multiplier_12_out), .out(adder_11_out), .cout(ad8));  // open: cin
  Adder adder_12 (.a(multiplier_13_out), .b(multiplier_14_out), .out(adder_12_out), .cout(ad9));  // open: cin
  Adder adder_13 (.a(multiplier_15_out), .b(multiplier_16_out), .out(adder_13_out), .cout(ad10));  // open: cin
  Multiplexer #(.width(8)) multiplexer_1 (.in0(adder_9_out), .in1({8{1'b1}}), .out(multiplexer_1_out), .sel(op_or));
  Adder adder_14 (.a(adder_10_out), .b(adder_11_out), .out(adder_14_out), .cout(ad11));  // open: cin
  Adder adder_15 (.a(adder_12_out), .b(adder_13_out), .out(adder_15_out), .cout(ad12));  // open: cin
  Adder adder_16 (.a(adder_14_out), .b(adder_15_out), .out(adder_16_out), .cout(ad13));  // open: cin
  Register register_1 (.D(multiplexer_1_out), .en(1'b1), .clk(latch), .Q(opt), .clr(en_bar));
  // Probe on opt
endmodule

module main_2 (
);

  wire [7:0] op0, op1, op2, op3, op4, op5, op6, op7, op8, op9, op10, op11, op12, op13, op14, op15;

  mac_p m0 (.opt(op0));  // open: w0, x0, w1, x1, b, latch, en_bar
  mac_p m4 (.opt(op4));  // open: w0, x0, w1, x1, b, latch, en_bar
  mac_p m8 (.opt(op8));  // open: w0, x0, w1, x1, b, latch, en_bar
  mac_p m12 (.opt(op12));  // open: w0, x0, w1, x1, b, latch, en_bar
  mac_p m1 (.opt(op1));  // open: w0, x0, w1, x1, b, latch, en_bar
  mac_p m5 (.opt(op5));  // open: w0, x0, w1, x1, b, latch, en_bar
  mac_p m9 (.opt(op9));  // open: w0, x0, w1, x1, b, latch, en_bar
  mac_p m13 (.opt(op13));  // open: w0, x0, w1, x1, b, latch, en_bar
  mac_p m2 (.opt(op2));  // open: w0, x0, w1, x1, b, latch, en_bar
  mac_p m6 (.opt(op6));  // open: w0, x0, w1, x1, b, latch, en_bar
  mac_p m10 (.opt(op10));  // open: w0, x0, w1, x1, b, latch, en_bar
  mac_p m14 (.opt(op14));  // open: w0, x0, w1, x1, b, latch, en_bar
  mac_p m3 (.opt(op3));  // open: w0, x0, w1, x1, b, latch, en_bar
  mac_p m7 (.opt(op7));  // open: w0, x0, w1, x1, b, latch, en_bar
  mac_p m11 (.opt(op11));  // open: w0, x0, w1, x1, b, latch, en_bar
  mac_p m15 (.opt(op15));  // open: w0, x0, w1, x1, b, latch, en_bar
endmodule
